# Fritzing sketch esquema cableado fritzing 2 gears (saved by Fritzing 1.0.7)
stripboards: 1

parts:
  part = shaft encoder  # not connected
  C1 = Electrolytic Capacitor [capacitance=100nF voltage=35V package="100 mil [THT, electrolytic]"]  # not connected
  Encoder_Derecho = shaft encoder  # not connected
  C2 = Electrolytic Capacitor [capacitance=100nF voltage=35V package="100 mil [THT, electrolytic]"]  # not connected
  S1 = H-Bridge with L298N
  DERECHA = gear-motor [part_number=ENB]
  HC-SR04_Sensor_1 = HC-SR04 Ultrasonic Distance Sensor  # not connected
  IZQUIERDA = gear-motor [part_number=ENA]
  part_2 = Camdenboss CTB0158-11 [part_number=GND package=THT]
  VCC2 = Camdenboss CTB0158-11 [part_number=5v package=THT]
  VCC3 = 4 x AAA Battery Mount [internal_resistance=0.1Ω]
  Componente1 = Arduino Nano (Rev3.0)  # not connected
  Componente2 = Bluetooth HC-05 Macho
  R1 = Resistor [tolerance=±5% resistance=2.2k part_number="2K oms" package="2010 [SMD]"]  # not connected
  M1 = Dagu DGServo 9g (Top view) [part_number=SG90]
  part_3 = Capacitor Polarized [part_number="100-470 pico" package=panasonic_d]
  part_4 = Capacitor Polarized [part_number="0.1 pico" package=panasonic_d]  # not connected
  part_5 = RioRand LM2596 [part_number="12v >> 5v"]
  VCC = Camdenboss CTB0158-4 [part_number=12v package=THT]

nets:
  N1: S1.12V, VCC.pin3
  N2: S1.GND, part_2.pin1
  N3: S1.5V, VCC2.pin11
  N4: S1.M1-01, IZQUIERDA.pin_2
  N5: S1.M1-02, IZQUIERDA.pin_1
  N6: S1.M2-01, DERECHA.pin_2
  N7: S1.M2-02, DERECHA.pin_1
  N8: part_2.pin2, VCC3.-
  N9: part_2.pin6, Componente2.GND
  N10: part_2.pin7, part_5.Pin_4
  N11: part_2.pin8, part_5.Pin_2
  N12: VCC2.pin6, Componente2.VCC
  N13: VCC3.+, VCC.pin1
  N14: M1.gnd, part_3.-
  N15: M1.vcc, part_3.+
  N16: part_5.Pin_1, VCC.pin2

notes:
  OUT1 rojo
  OUT2 GND
  OUT3 rojo
  OUT4 GND

custom parts:
  H-Bridge with L298N: h-bridge
  gear-motor: Generic gear motor, 3V to 6V, dual output shafts, 1:48 gear ratio.
