# Fritzing sketch galletitaMoves - esquema cableado fritzing (saved by Fritzing 0.9.10b)
breadboards: 1

parts:
  Encoder_Izquierdo = shaft encoder  # not connected
  C1 = Electrolytic Capacitor [capacitance=100nF voltage=35V package="100 mil [THT, electrolytic]"]  # not connected
  Encoder_Derecho = shaft encoder  # not connected
  C2 = Electrolytic Capacitor [capacitance=100nF voltage=35V package="100 mil [THT, electrolytic]"]  # not connected
  S1 = H-Bridge with L298N
  TRASERA_DERECHA = gear-motor
  DELANTERA_DERECHA = gear-motor
  VCC1 = 4 x AAA Battery Mount
  HC-SR04_Sensor_1 = HC-SR04 Ultrasonic Distance Sensor  # not connected
  A1 = Arduino UNO R4 WiFi
  BAT1 = Battery Holders [package=battery-aa-kit]  # not connected
  TRASERA_IZQDA = gear-motor
  DELANTERA_IZDA = gear-motor
  J1 = Basic Servo  # not connected
  C3 = Electrolytic Capacitor [capacitance=100nF voltage=35V package="100 mil [THT, electrolytic]"]  # not connected

nets:
  N1: S1.GND, VCC1.-
  N2: S1.ENA, S1.ENA-5V
  N3: S1.ENB, S1.ENB-5V
  N4: S1.M1-01, TRASERA_IZQDA.pin_2, DELANTERA_IZDA.pin_2
  N5: S1.M1-02, TRASERA_IZQDA.pin_1, DELANTERA_IZDA.pin_1
  N6: S1.M2-01, TRASERA_DERECHA.pin_2, DELANTERA_DERECHA.pin_2
  N7: S1.M2-02, TRASERA_DERECHA.pin_1, DELANTERA_DERECHA.pin_1
  N8: VCC1.+, A1.Pin_11

notes:
  OUT1 rojo
  OUT2 GND
  OUT3 rojo
  OUT4 GND
  5v
  12v

custom parts:
  H-Bridge with L298N: h-bridge
  gear-motor: Generic gear motor, 3V to 6V, dual output shafts, 1:48 gear ratio.
  Arduino UNO R4 WiFi: The Arduino UNO R4 WiFi merges the RA4M1 microprocessor from Renesas with the ESP32-S3 from Espressif, creating an all-in-one tool for makers with enhanced processing power and a diverse array of new peripherals.
